# Fritzing sketch zigbee-usb-switch (saved by Fritzing 0.9.5d)
breadboards: 1

parts:
  A1 = ESP32-C6-DevKitC-1
  U1 = Sharp PC817 [package=THT]
  R1 = Resistor [tolerance=±5% resistance=330 package=THT]
  LED1 = LED - 5mm [color="Red (633nm)" package="5 mm [THT]"]
  U2 = Sharp PC817 [package=THT]
  R2 = Resistor [tolerance=±5% resistance=330 package=THT]
  LED2 = LED - 5mm [color="Red (633nm)" package="5 mm [THT]"]
  U3 = Sharp PC817 [package=THT]
  R3 = Resistor [tolerance=±5% resistance=330 package=THT]
  S1 = Pushbutton [package="[THT]"]
  V1 = DC Power [voltage=2.75V]
  V2 = DC Power [voltage=2.75V]
  V3 = DC Power [voltage=5]

nets:
  GND: A1.Pin_15, A1.Pin_18, A1.Pin_32, U1.Pin_2, U1.Pin_3, LED1.cathode, U2.Pin_2, U2.Pin_3, LED2.cathode, U3.Pin_2, U3.Pin_3, S1.Pin_1, S1.Pin_2, V1.V-, V2.V-, V3.V-
  N1: A1.Pin_23, U2.Pin_4
  N2: A1.Pin_24, U1.Pin_4
  N3: A1.Pin_25, R3.Pin_0
  N4: U1.Pin_1, R1.Pin_1
  N5: R1.Pin_0, LED1.anode, V2.V+
  N6: U2.Pin_1, R2.Pin_1
  N7: R2.Pin_0, LED2.anode, V1.V+
  N8: U3.Pin_1, R3.Pin_1
  N9: U3.Pin_4, S1.Pin_3, S1.Pin_4, V3.V+

custom parts:
  ESP32-C6-DevKitC-1: ESP32-C6-DevKitC-1 is an entry-level development board based on ESP32-C6-WROOM-1(U), a general-purpose module with a 8 MB SPI flash. This board integrates complete Wi-Fi, Bluetooth LE, Zigbee, and Thread functions.
